# Fritzing sketch AutoTea (saved by Fritzing 0.9.3b)
breadboards: 1

parts:
  Part1 = Arduino Mega 2560 (Rev3)
  U2 = LCD-16X2 [package=lcd-16x2]
  S1 = Pushbutton [package="[SMD]"]
  U1 = POT [package=pot_alpha_rv16af-20]
  J1 = Basic Servo
  Water_Sensor = hc-sr04
  Cup_Sensor = hc-sr04  # not connected
  LED1 = RGB LED - (4 legs) [package="5 mm [THT]"]
  Stepper_Driver_Board = ULN2003A - Stepper Driver Board [package=board]

nets (from the breadboard view):
  N1: Part1.D13_PWM, Water_Sensor.Trig
  N2: Part1.D12_PWM, U2.DB7
  N3: Part1.D11_PWM, U2.DB6
  N4: Part1.D10_PWM, U2.DB5
  N5: Part1.D9_PWM, U2.DB3, U2.DB4
  N6: Part1.D8_PWM, U2.E
  VCC: Part1.5V, U2.VDD, U2.A, U1.E, J1.vcc, Water_Sensor.VCC, LED1.common_anode, Stepper_Driver_Board.VCC
  GND: Part1.GND, Part1.D53, U2.VSS, U2.K, S1.Pin_3, S1.Pin_4, U1.A, J1.gnd, Water_Sensor.GND, Stepper_Driver_Board.GND
  N7: Part1.D2_PWM, Stepper_Driver_Board.IN1
  N8: Part1.D3_PWM, Stepper_Driver_Board.IN3
  N9: Part1.D4_PWM, Stepper_Driver_Board.IN2
  N10: Part1.D5_PWM, Stepper_Driver_Board.IN4
  N11: Part1.D6_PWM, Water_Sensor.Echo
  N12: Part1.D7_PWM, U2.RS, U2.R_W
  N13: Part1.D48, LED1.blue_cathode
  N14: Part1.D50, LED1.green_cathode
  N15: Part1.D51, J1.pulse
  N16: Part1.D52, LED1.red_cathode
  N17: U2.VO, U1.S

custom parts:
  ULN2003A - Stepper Driver Board: A common stepper motor driver board based on ULN2003APG darlington array
